// Logisim project ALU__Control.circ as structural Verilog: 1 circuit, main circuit ALU_control
module ALU_control (
  input  [5:0] Instruction,
  input  [2:0] ALU_op,
  output [5:0] ALU_code
);

  Multiplexer #(.select(3), .width(6), .enable("false")) multiplexer_1 (
    .in0(Instruction), .in1({6{1'b0}}), .in2(6'b000100), .in3(6'b000101), .in4(6'b000011), .in5(6'b110011),
    .in6(6'b000110), .in7({6{1'b0}}), .out(ALU_code), .sel(ALU_op));
endmodule
